# Fritzing sketch WireGame 2 (saved by Fritzing 0.9.10b)
breadboards: 3

parts:
  Part1 = Adafruit Mini TFT Display - 0.96in 160x80 [part_number="Adafruit 3533"]
  S1 = Pushbutton [package="[SMD]"]
  S2 = Pushbutton [package="[SMD]"]
  S3 = Pushbutton [package="[SMD]"]
  Part2 = Adafruit ESP32-S3 Feather [part_number="Adafruit #5323"]
  ZS-042_RTC1 = ZS-042 RTC Module  # not connected
  J1 = Piezo Speaker
  R1 = Resistor [tolerance=±5% resistance=68 package="0603 [SMD]"]
  S4 = Pushbutton [package="[THT]"]
  S5 = Pushbutton [package="[THT]"]

nets:
  N1: Part1.VIN, Part2.VBUS
  GND: Part1.GND, S1.Pin_1, S1.Pin_2, S2.Pin_1, S2.Pin_2, S3.Pin_1, S3.Pin_2, Part2.GND, J1.pin1
  N2: Part1.SCK, Part2.SCK
  N3: Part1.MISO, Part2.MISO
  N4: Part1.MOSI, Part2.MOSI
  N5: Part1.TFTCS, Part2.A5
  N6: Part1.TFTRST, Part2.A4
  N7: Part1.DC, Part2.A3
  N8: Part1.SDCS, Part2.A2
  N9: S1.Pin_3, S1.Pin_4, Part2.D9
  N10: S2.Pin_3, S2.Pin_4, Part2.D10
  N11: S3.Pin_3, S3.Pin_4, Part2.D6
  N12: Part2.D11, S5.Pin_3, S5.Pin_4
  N13: Part2.D5, S4.Pin_3, S4.Pin_4
  N14: J1.pin2, R1.Pin_1
  N15: S4.Pin_1, S4.Pin_2
  N16: S5.Pin_1, S5.Pin_2

notes:
  OK
  UP
  DOWN
  GAME WON
  TOUCHING WIRE
  Wire indicating the holder

custom parts:
  Adafruit Mini TFT Display - 0.96in 160x80: It's the size of your thumbnail, with glorious 160x80 pixel color... it's the Adafruit Mini TFT Breakout! This very very small display is only 0.96" diagonal, packed with RGB pixels, for making very small high-density displays. The display uses 4-wire SPI to communicate and has its own pixel-addressable frame buffer, it can be used with every kind of microcontroller. Even a very small one with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
  Adafruit ESP32-S3 Feather: The ESP32-S3 has arrived in Feather format - and what a great way to get started with this powerful new chip from Espressif! With dual 240 MHz cores, WiFi and BLE support, and native USB, this Feather is great for powering your IoT projects. That's right - it's the new Adafruit ESP32-S3 Feather! With native USB and 8 MB flash, this board will let you upgrade your existing ESP32 projects.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
